// Digital circuit Contador.dig as structural Verilog
module Contador (
  input  A5,
  input  A4,
  input  A3,
  input  A2,
  input  A1,
  input  A0,
  input  A_S,
  input  CLK,
  output LED
);

  wire add_1_s, add_2_c_o, add_2_s, add_3_c_o, add_3_s, add_4_c_o, add_4_s, add_5_c_o, add_5_s, add_6_c_o,
       add_6_s, d_ff_2_q, d_ff_3_q, d_ff_4_q, d_ff_5_q, d_ff_6_q, xor_1_out, xor_2_out, xor_3_out, xor_4_out,
       xor_5_out, xor_6_out;

  xor xor_1 (xor_1_out, A5, A_S);
  xor xor_2 (xor_2_out, A4, A_S);
  xor xor_3 (xor_3_out, A3, A_S);
  xor xor_4 (xor_4_out, A2, A_S);
  xor xor_5 (xor_5_out, A1, A_S);
  xor xor_6 (xor_6_out, A0, A_S);
  Add add_1 (.a(LED), .b(xor_1_out), .c_i(add_2_c_o), .s(add_1_s));  // open: c_o
  Add add_2 (.a(d_ff_2_q), .b(xor_2_out), .c_i(add_3_c_o), .s(add_2_s), .c_o(add_2_c_o));
  Add add_3 (.a(d_ff_3_q), .b(xor_3_out), .c_i(add_4_c_o), .s(add_3_s), .c_o(add_3_c_o));
  Add add_4 (.a(d_ff_4_q), .b(xor_4_out), .c_i(add_5_c_o), .s(add_4_s), .c_o(add_4_c_o));
  Add add_5 (.a(d_ff_5_q), .b(xor_5_out), .c_i(add_6_c_o), .s(add_5_s), .c_o(add_5_c_o));
  Add add_6 (.a(d_ff_6_q), .b(xor_6_out), .c_i(A_S), .s(add_6_s), .c_o(add_6_c_o));
  D_FF d_ff_1 (.D(add_1_s), .C(CLK), .Q(LED));  // open: nQ
  D_FF d_ff_2 (.D(add_2_s), .C(CLK), .Q(d_ff_2_q));  // open: nQ
  D_FF d_ff_3 (.D(add_3_s), .C(CLK), .Q(d_ff_3_q));  // open: nQ
  D_FF d_ff_4 (.D(add_4_s), .C(CLK), .Q(d_ff_4_q));  // open: nQ
  D_FF d_ff_5 (.D(add_5_s), .C(CLK), .Q(d_ff_5_q));  // open: nQ
  D_FF d_ff_6 (.D(add_6_s), .C(CLK), .Q(d_ff_6_q));  // open: nQ
endmodule

/* Test case TB:
A/S A5 A4 A3 A2 A1 A0 CLK LED
 0  1  0  0  0  0  0   C   1 
 0  0  0  0  0  0  0   C   0  
 1  1  0  0  0  0  0   C   0  
 0  0  0  0  0  0  1   C   0  
*/
